// Logisim project DEC.circ as structural Verilog: 1 circuit, main circuit dec_cu
module dec_cu (
  input  [3:0] flag_in,
  output NOP_op,
  output STA_op,
  output LDA_op,
  output ADD_op,
  output OR_op,
  output AND_op,
  output NOT_op,
  output JMP_op,
  output JN_op,
  output JZ_op,
  output HLT_op
);

  wire and_1_out, and_2_out, and_3_out, and_4_out, and_5_out, and_6_out, and_7_out, and_8_out, and_9_out,
       and_10_out, and_11_out, and_12_out, and_13_out, and_14_out, and_15_out, and_16_out, and_17_out,
       and_18_out, and_19_out, and_20_out, and_21_out, and_22_out, not_1_out, not_2_out, not_3_out, not_4_out;

  not not_1 (not_1_out, flag_in[3]);
  not not_2 (not_2_out, flag_in[2]);
  not not_3 (not_3_out, flag_in[1]);
  not not_4 (not_4_out, flag_in[0]);
  and and_1 (and_1_out, not_1_out, not_2_out);
  and and_2 (and_2_out, not_3_out, not_4_out);
  and and_3 (and_3_out, not_1_out, not_2_out);
  and and_4 (and_4_out, not_3_out, flag_in[0]);
  and and_5 (and_5_out, not_1_out, not_2_out);
  and and_6 (and_6_out, flag_in[1], not_4_out);
  and and_7 (and_7_out, not_1_out, not_2_out);
  and and_8 (and_8_out, flag_in[1], flag_in[0]);
  and and_9 (and_9_out, not_1_out, flag_in[2]);
  and and_10 (and_10_out, not_3_out, not_4_out);
  and and_11 (and_11_out, not_1_out, flag_in[2]);
  and and_12 (and_12_out, not_3_out, flag_in[0]);
  and and_13 (and_13_out, not_1_out, flag_in[2]);
  and and_14 (and_14_out, flag_in[1], not_4_out);
  and and_15 (and_15_out, flag_in[3], not_2_out);
  and and_16 (and_16_out, not_3_out, not_4_out);
  and and_17 (and_17_out, flag_in[3], not_2_out);
  and and_18 (and_18_out, not_3_out, flag_in[0]);
  and and_19 (and_19_out, flag_in[3], not_2_out);
  and and_20 (and_20_out, flag_in[1], not_4_out);
  and and_21 (and_21_out, flag_in[3], flag_in[2]);
  and and_22 (and_22_out, flag_in[1], flag_in[0]);
  and and_23 (NOP_op, and_1_out, and_2_out);
  and and_24 (STA_op, and_3_out, and_4_out);
  and and_25 (LDA_op, and_5_out, and_6_out);
  and and_26 (ADD_op, and_7_out, and_8_out);
  and and_27 (OR_op, and_9_out, and_10_out);
  and and_28 (AND_op, and_11_out, and_12_out);
  and and_29 (NOT_op, and_13_out, and_14_out);
  and and_30 (JMP_op, and_15_out, and_16_out);
  and and_31 (JN_op, and_17_out, and_18_out);
  and and_32 (JZ_op, and_19_out, and_20_out);
  and and_33 (HLT_op, and_21_out, and_22_out);
endmodule
