// Logisim project PC.circ as structural Verilog: 1 circuit, main circuit program_counter
module program_counter (
  input  cargaPC,
  input  incPC,
  input  clock,
  input  reset,
  input  [7:0] Pinp,
  output [7:0] Count
);

  Counter PC (.clr(reset), .load(cargaPC), .up(incPC), .count(incPC), .clk(clock), .D(Pinp), .Q(Count));  // open: carry
endmodule
