// Logisim project acumulador.circ as structural Verilog: 1 circuit, main circuit ACC
module ACC (
  input  [7:0] data_input,
  input  enable,
  input  clock,
  input  reset,
  output [7:0] data_output
);

  Register register_1 (.D(data_input), .en(enable), .clk(clock), .Q(data_output), .clr(reset));
endmodule
