// Logisim project adder8bits.circ as structural Verilog: 1 circuit, main circuit adder_8bits
module adder_8bits (
  input  [7:0] input_a,
  input  [7:0] input_b,
  output [7:0] output_s
);

  wire adder_1_cout;

  Adder adder_1 (.a(input_a), .b(input_b), .out(output_s), .cin(1'b0), .cout(adder_1_cout));
  // also tied to GND on the sheet: adder_1_cout
endmodule
