// Logisim project and_8_bits.circ as structural Verilog: 1 circuit, main circuit and_8_bits
module and_8_bits (
  input  [7:0] input_a,
  input  [7:0] input_b,
  output [7:0] output_s
);

  assign output_s = input_a & input_b;  // AND_Gate and_1, 8 bits wide
endmodule
