// Logisim project control_unity.circ as structural Verilog: 1 circuit, main circuit control_un
module control_un (
  input  NOP_op,
  input  STA_op,
  input  LDA_op,
  input  ADD_op,
  input  OR_op,
  input  AND_op,
  input  NOT_op,
  input  JMP_op,
  input  JN_op,
  input  JZ_op,
  input  HLT_op,
  input  N,
  input  Z,
  input  clock,
  output goto0,
  output cargaPC,
  output cargaNZ,
  output cargaAC,
  output ulaNOT,
  output ulaAND,
  output ulaOR,
  output ulaADD,
  output ulaY,
  output write,
  output read,
  output cargaRDM,
  output sel,
  output incPC,
  output cargaRI,
  output cargaREM
);

  wire and_1_out, and_2_out, and_3_out, and_4_out, and_5_out, and_6_out, and_8_out, and_9_out, and_16_out,
       JNc_out, JNZc_out, JZc_out, LDA_ADD_OR_AND_out, Nc_out, not_1_out, not_2_out, or_1_out, or_2_out,
       or_3_out, or_4_out, STA_LDA_ADD_OR_AND_JMP_JNN_JZZ_out, t4_mais_N_out, temp_sinal_1_p1,
       temp_sinal_1_p2, temp_sinal_1_p3, temp_sinal_1_p4, temp_sinal_1_p5, temp_sinal_1_p9, temp_sinal_1_p11,
       Zc_out;

  not not_1 (not_1_out, N);
  not not_2 (not_2_out, Z);
  and JZc (JZc_out, not_2_out, JZ_op);
  and JNc (JNc_out, not_1_out, JN_op);
  and Zc (Zc_out, Z, JZ_op);
  and Nc (Nc_out, N, JN_op);
  or STA_LDA_ADD_OR_AND_JMP_JNN_JZZ (STA_LDA_ADD_OR_AND_JMP_JNN_JZZ_out, Zc_out, STA_op, JMP_op, Nc_out, LDA_ADD_OR_AND_out);
  and and_1 (and_1_out, STA_LDA_ADD_OR_AND_JMP_JNN_JZZ_out, temp_sinal_1_p4);
  or or_1 (or_1_out, STA_op, LDA_op, ADD_op, OR_op, AND_op);
  or LDA_ADD_OR_AND (LDA_ADD_OR_AND_out, LDA_op, ADD_op, OR_op, AND_op);
  and and_2 (and_2_out, LDA_ADD_OR_AND_out, temp_sinal_1_p2);
  or or_2 (or_2_out, JNc_out, JZc_out);
  and and_3 (and_3_out, or_2_out, temp_sinal_1_p5);
  and and_4 (and_4_out, STA_LDA_ADD_OR_AND_JMP_JNN_JZZ_out, temp_sinal_1_p5);
  or JNZc (JNZc_out, JNc_out, JZc_out, NOP_op, NOT_op);
  or or_3 (or_3_out, Nc_out, Zc_out, JMP_op);
  or or_4 (or_4_out, STA_op, LDA_op, ADD_op, OR_op);
  // temp_sinal temp_sinal_1: pin names not known; wires that end beside it: temp_sinal_1_p1, temp_sinal_1_p2, temp_sinal_1_p3, temp_sinal_1_p4, temp_sinal_1_p5, goto0, cargaRI, clock, temp_sinal_1_p9, HLT_op, temp_sinal_1_p11
  and and_5 (and_5_out, temp_sinal_1_p1, or_1_out);
  and and_6 (and_6_out, temp_sinal_1_p5, JNZc_out);
  and and_7 (cargaPC, temp_sinal_1_p3, or_3_out);
  and and_8 (and_8_out, temp_sinal_1_p1, or_4_out);
  and and_9 (and_9_out, temp_sinal_1_p5, NOT_op);
  and and_10 (ulaNOT, temp_sinal_1_p5, NOT_op);
  and and_11 (ulaAND, temp_sinal_1_p1, AND_op);
  and and_12 (ulaOR, temp_sinal_1_p1, OR_op);
  and and_13 (ulaADD, temp_sinal_1_p1, ADD_op);
  and and_14 (ulaY, temp_sinal_1_p1, LDA_op);
  and and_15 (write, temp_sinal_1_p1, STA_op);
  or or_5 (read, temp_sinal_1_p9, and_2_out, and_1_out);
  and and_16 (and_16_out, temp_sinal_1_p2, STA_op);
  and and_17 (sel, temp_sinal_1_p3, or_1_out);
  and t4_mais_N (t4_mais_N_out, temp_sinal_1_p4, or_1_out);
  or or_6 (cargaAC, and_8_out, and_9_out);
  or or_7 (cargaRDM, read, and_16_out);
  or or_8 (incPC, t4_mais_N_out, and_3_out, temp_sinal_1_p9);
  or or_9 (goto0, and_5_out, and_6_out, cargaPC);
  or or_10 (cargaREM, sel, and_4_out, temp_sinal_1_p11);

  assign cargaNZ = cargaAC;
endmodule
