// Logisim project control_unity_2.0.circ as structural Verilog: 1 circuit, main circuit control_unity_v2
module control_unity_v2 (
  input  NOP_op,
  input  STA_op,
  input  LDA_op,
  input  ADD_op,
  input  OR_op,
  input  AND_op,
  input  NOT_op,
  input  JMP_op,
  input  JN_op,
  input  JZ_op,
  input  HLT_op,
  input  N,
  input  Z,
  input  clock,
  input  reset,
  output cargaPC,
  output cargaNZ,
  output cargaAC,
  output ulaNOT,
  output ulaAND,
  output ulaOR,
  output ulaADD,
  output ulaY,
  output write,
  output read,
  output cargaRDM,
  output sel,
  output incPC,
  output cargaRI,
  output cargaREM
);

  wire and_1_out, and_2_out, and_3_out, and_4_out, and_5_out, and_6_out, and_7_out, and_8_out, and_11_out,
       and_12_out, and_13_out, and_19_out, and_20_out, and_21_out, and_22_out, and_24_out, goto_tO, J, K,
       N_bar, or_11_out, reset_tO, t0, t1, t3, t4, t5, t6, t7, W, X, Y, Z_bar;

  and and_1 (and_1_out, JN_op, N);
  and and_2 (and_2_out, Z, JZ_op);
  and and_3 (and_3_out, JN_op, N_bar);
  and and_4 (and_4_out, Z_bar, JZ_op);
  or or_1 (X, Y, J);
  or or_2 (W, LDA_op, ADD_op, AND_op, OR_op);
  or or_3 (Y, W, STA_op);
  or or_4 (J, JMP_op, and_1_out, and_2_out);
  or or_5 (K, and_3_out, and_4_out);
  and and_5 (and_5_out, X, t3);
  and and_6 (and_6_out, Y, t5);
  and and_7 (and_7_out, K, t3);
  and and_8 (and_8_out, Y, t4);
  and and_9 (sel, Y, t5);
  or or_6 (cargaREM, and_5_out, and_6_out, t0);
  or or_7 (incPC, and_7_out, and_8_out, t1);
  and and_10 (ulaY, LDA_op, t7);
  and and_11 (and_11_out, X, t4);
  and and_12 (and_12_out, W, t6);
  and and_13 (and_13_out, STA_op, t6);
  not not_1 (N_bar, N);
  not not_2 (Z_bar, Z);
  or or_8 (read, and_11_out, and_12_out, t1);
  or or_9 (cargaRDM, and_13_out, read);
  and and_14 (write, STA_op, t7);
  and and_15 (ulaADD, ADD_op, t7);
  and and_16 (ulaOR, OR_op, t7);
  and and_17 (ulaAND, AND_op, t7);
  and and_18 (ulaNOT, NOT_op, t3);
  and and_19 (and_19_out, W, t7);
  and and_20 (and_20_out, NOT_op, t3);
  or or_10 (cargaAC, and_19_out, and_20_out);
  and and_21 (and_21_out, Y, t7);
  or or_11 (or_11_out, NOP_op, NOT_op, K);
  and and_22 (and_22_out, J, t5);
  and and_23 (cargaPC, J, t5);
  and and_24 (and_24_out, or_11_out, t3);
  or or_12 (goto_tO, and_21_out, and_24_out, and_22_out);
  temp_sinal temp_sinal_1 (
    .HLT(HLT_op), .goto0(goto_tO), .clock(clock), .reset(reset_tO), .t0(t0), .t1(t1), .t2(cargaRI), .t3(t3),
    .t4(t4), .t5(t5), .t6(t6), .t7(t7));
  LED led_1 (.in(t0));
  LED led_2 (.in(t1));
  LED led_3 (.in(cargaRI));
  LED led_4 (.in(t3));
  LED led_5 (.in(t4));
  LED led_6 (.in(t5));
  LED led_7 (.in(t6));
  LED led_8 (.in(t7));
  or or_13 (reset_tO, reset, goto_tO);

  assign cargaNZ = cargaAC;

  // Other names for the same wires on the sheet: t2 = cargaRI; ula_ADD = ulaADD; ula_AND = ulaAND; ula_NOT = ulaNOT;
  //   ula_OR = ulaOR; ula_Y = ulaY

  // Notes on the sheet:
  //   Interface de Entrada
  //   cargaREM
  //   incPC
  //   ula_Y
  //   sel
  //   cargaRDM
  //   write
  //   ula_ADD
  //   READ
  //   ula_OR
  //   ula_AND
  //   ula_NOT
  //   cargaAC
  //   cargaRI
  //   temp_counter
  //   cargaNZ
  //   cargaPC
  //   goto_tO
  //   PINOUT
  //   reset_tO
endmodule
