// Logisim project dec_count_c.circ as structural Verilog
module dec_count (
  input  N3,
  input  N2,
  input  N1,
  output S8,
  output S7,
  output S6,
  output S5,
  output S4,
  output S3,
  output S2,
  output S1
);

  wire and_1_out, and_2_out, and_3_out, and_4_out, and_5_out, and_6_out, and_7_out, and_8_out, not_1_out,
       not_2_out, not_3_out;

  not not_1 (not_1_out, N3);
  not not_2 (not_2_out, N2);
  not not_3 (not_3_out, N1);
  and and_1 (and_1_out, N3, N2);
  and and_2 (and_2_out, N3, N2);
  and and_3 (and_3_out, N3, not_2_out);
  and and_4 (and_4_out, N3, not_2_out);
  and and_5 (and_5_out, not_1_out, N2);
  and and_6 (and_6_out, not_1_out, N2);
  and and_7 (and_7_out, not_1_out, not_2_out);
  and and_8 (and_8_out, not_1_out, not_2_out);
  and and_9 (S8, and_1_out, N1);
  and and_10 (S7, and_2_out, not_3_out);
  and and_11 (S6, and_3_out, N1);
  and and_12 (S5, and_4_out, not_3_out);
  and and_13 (S4, and_5_out, N1);
  and and_14 (S3, and_6_out, not_3_out);
  and and_15 (S2, and_7_out, N1);
  and and_16 (S1, and_8_out, not_3_out);
endmodule
