// Logisim project disp7s.circ as structural Verilog: 1 circuit, main circuit disp7seg
module disp7seg (
  input  A,
  input  B,
  input  C,
  input  D,
  output a_o,
  output b_o,
  output c_o,
  output d_o,
  output e_o,
  output f_o,
  output g_o
);

  wire and_1_out, and_2_out, and_3_out, and_4_out, and_5_out, and_6_out, and_7_out, and_8_out, and_9_out,
       and_10_out, and_11_out, and_12_out, and_13_out, and_14_out, and_15_out, and_16_out, and_17_out,
       and_18_out, and_19_out, and_20_out, and_21_out, and_22_out, and_23_out, and_24_out, and_25_out,
       and_26_out, and_27_out, and_28_out, and_29_out, and_30_out, and_31_out, and_32_out, and_33_out,
       and_34_out, and_35_out, and_36_out, and_37_out, and_38_out, and_39_out, and_40_out, and_41_out,
       and_42_out, and_43_out, and_44_out, and_45_out, not_1_out, not_2_out, not_3_out, not_4_out, or_1_out,
       or_2_out, or_4_out, or_5_out, or_7_out, or_9_out, or_11_out, or_13_out, or_15_out, or_16_out,
       or_18_out;

  not not_1 (not_1_out, A);
  not not_2 (not_2_out, B);
  not not_3 (not_3_out, C);
  not not_4 (not_4_out, D);
  and and_1 (and_1_out, not_1_out, B);
  and and_2 (and_2_out, A, not_2_out);
  and and_3 (and_3_out, not_1_out, not_2_out);
  and and_4 (and_4_out, not_1_out, not_3_out);
  and and_5 (and_5_out, not_1_out, C);
  and and_6 (and_6_out, not_1_out, D);
  and and_7 (and_7_out, not_1_out, B);
  and and_8 (and_8_out, not_1_out, not_2_out);
  and and_9 (and_9_out, not_1_out, B);
  and and_10 (and_10_out, not_3_out, D);
  and and_11 (and_11_out, not_1_out, C);
  and and_12 (and_12_out, not_2_out, not_3_out);
  and and_13 (and_13_out, not_1_out, C);
  and and_14 (and_14_out, not_2_out, not_3_out);
  and and_15 (and_15_out, not_1_out, B);
  and and_16 (and_16_out, not_1_out, B);
  and and_17 (and_17_out, A, not_2_out);
  and and_18 (and_18_out, not_1_out, not_3_out);
  and and_19 (and_19_out, not_1_out, not_2_out);
  and and_20 (and_20_out, not_1_out, B);
  and and_21 (and_21_out, A, not_2_out);
  and and_22 (and_22_out, not_1_out, C);
  and and_23 (and_23_out, not_1_out, C);
  and and_24 (and_24_out, and_1_out, D);
  and and_25 (and_25_out, and_2_out, not_3_out);
  and and_26 (and_26_out, and_3_out, not_4_out);
  and and_27 (and_27_out, not_1_out, not_2_out);
  and and_28 (and_28_out, and_4_out, not_4_out);
  and and_29 (and_29_out, and_5_out, D);
  and and_30 (and_30_out, not_2_out, not_3_out);
  or or_1 (or_1_out, and_6_out, and_7_out);
  and and_31 (and_31_out, not_2_out, not_3_out);
  and and_32 (and_32_out, and_8_out, C);
  and and_33 (and_33_out, and_9_out, and_10_out);
  and and_34 (and_34_out, and_11_out, not_4_out);
  and and_35 (and_35_out, and_12_out, not_4_out);
  and and_36 (and_36_out, and_13_out, not_4_out);
  and and_37 (and_37_out, and_14_out, not_4_out);
  and and_38 (and_38_out, and_15_out, not_3_out);
  and and_39 (and_39_out, and_16_out, not_4_out);
  and and_40 (and_40_out, and_17_out, not_3_out);
  and and_41 (and_41_out, and_18_out, not_4_out);
  and and_42 (and_42_out, and_19_out, C);
  and and_43 (and_43_out, and_20_out, not_3_out);
  and and_44 (and_44_out, and_21_out, not_3_out);
  and and_45 (and_45_out, and_22_out, not_4_out);
  or or_2 (or_2_out, and_23_out, and_24_out);
  or or_3 (a_o, or_2_out, or_4_out);
  or or_4 (or_4_out, and_25_out, and_26_out);
  or or_5 (or_5_out, and_27_out, and_28_out);
  or or_6 (b_o, or_5_out, or_7_out);
  or or_7 (or_7_out, and_29_out, and_30_out);
  or or_8 (c_o, or_1_out, and_31_out);
  or or_9 (or_9_out, and_32_out, and_33_out);
  or or_10 (d_o, or_9_out, or_11_out);
  or or_11 (or_11_out, and_34_out, and_35_out);
  or or_12 (e_o, and_36_out, and_37_out);
  or or_13 (or_13_out, and_38_out, and_39_out);
  or or_14 (f_o, or_13_out, or_15_out);
  or or_15 (or_15_out, and_40_out, and_41_out);
  or or_16 (or_16_out, and_42_out, and_43_out);
  or or_17 (g_o, or_16_out, or_18_out);
  or or_18 (or_18_out, and_44_out, and_45_out);
endmodule
