// Logisim project doubledisp.circ as structural Verilog: 1 circuit, main circuit div2disp
module div2disp (
  input  n_3,
  input  n_2,
  input  n_1,
  input  n_0,
  output dez_a,
  output dez_b,
  output dez_c,
  output dez_d,
  output dez_e,
  output dez_f,
  output dez_g,
  output un_a,
  output un_b,
  output un_c,
  output un_d,
  output un_e,
  output un_f,
  output un_g
);

  wire [3:0] divider_1_out, divider_1_rem;

  Divider #(.width(4)) divider_1 (
    .a({n_3, n_2, n_1, n_0}), .b(4'b1010), .out(divider_1_out), .rem(divider_1_rem));  // open: upper
  disp7seg disp7seg_1 (
    .A(divider_1_rem[3]), .B(divider_1_rem[2]), .C(divider_1_rem[1]), .D(divider_1_rem[0]), .a_o(un_a),
    .b_o(un_b), .c_o(un_c), .d_o(un_d), .e_o(un_e), .f_o(un_f), .g_o(un_g));
  disp7seg disp7seg_2 (
    .A(divider_1_out[3]), .B(divider_1_out[2]), .C(divider_1_out[1]), .D(divider_1_out[0]), .a_o(dez_a),
    .b_o(dez_b), .c_o(dez_c), .d_o(dez_d), .e_o(dez_e), .f_o(dez_f), .g_o(dez_g));
endmodule
