// Logisim project mem_ram.circ as structural Verilog: 1 circuit, main circuit MEM
module MEM (
  input  [7:0] address_i,
  input  write,
  input  read,
  input  clk,
  input  [7:0] data_in,
  output [7:0] data_out,
  output selRDM
);

  RAM #(.asyncread("true")) ram_1 (.addr(address_i), .we(write), .oe(read), .clk(clk), .din(data_in), .dout(data_out));

  assign selRDM = read;
endmodule
