// Logisim project mux8bits.circ as structural Verilog: 1 circuit, main circuit mux_8bits
module mux_8bits (
  input  [7:0] inp_1,
  input  [7:0] inp_2,
  input  sel,
  output [7:0] out_mux
);

  Multiplexer #(.width(8)) multiplexer_1 (.in0(inp_1), .in1(inp_2), .out(out_mux), .sel(sel));
endmodule
