// Logisim project not_8_bits.circ as structural Verilog: 1 circuit, main circuit not_8_bits
module not_8_bits (
  input  [7:0] in_1,
  output [7:0] out_2
);

  assign out_2 = ~in_1;  // NOT_Gate not_1, 8 bits wide
endmodule
