// Logisim project op_cde.circ as structural Verilog: 1 circuit, main circuit opcode
module opcode (
  input  [7:0] data_input,
  input  cargaRI,
  input  clock,
  input  reset,
  output [3:0] flag_out
);

  wire [3:0] acc_1_data_output;

  ACC acc_1 (
    .data_input(data_input), .enable(cargaRI), .clock(clock), .reset(reset),
    .data_output({flag_out, acc_1_data_output}));
endmodule
