// Logisim project or_8_bits.circ as structural Verilog: 1 circuit, main circuit or_8_bits
module or_8_bits (
  input  [7:0] input_a,
  input  [7:0] input_b,
  output [7:0] output_s
);

  assign output_s = input_a | input_b;  // OR_Gate or_1, 8 bits wide
endmodule
