// Logisim project reg_NZ.circ as structural Verilog: 1 circuit, main circuit regNZ
module regNZ (
  input  enable,
  input  clock,
  input  reset,
  input  N_i,
  input  Z_i,
  output N_o,
  output Z_o
);

  Register #(.width(1)) register_1 (.D(N_i), .en(enable), .clk(clock), .Q(N_o), .clr(reset));
  Register #(.width(1)) register_2 (.D(Z_i), .en(enable), .clk(clock), .Q(Z_o), .clr(reset));
endmodule
