// Logisim project temp_sinal_gen.circ as structural Verilog: 1 circuit, main circuit temp_sinal
module temp_sinal (
  input  HLT,
  input  clock,
  input  goto0,
  output t0,
  output t1,
  output t2,
  output t3,
  output t4,
  output t5,
  output t6,
  output t7
);

  wire d_ff_1_q, d_ff_2_q, not_1_out;
  wire [2:0] counter_1_q;

  D_Flip_Flop d_ff_1 (.D(goto0), .clk(clock), .Q(d_ff_1_q));  // open: Qn, preset, reset
  Counter #(.max('h7), .width(3)) counter_1 (
    .clr(d_ff_2_q), .up(1'b1), .count(1'b1), .clk(clock), .Q(counter_1_q));  // open: load, D, carry
  D_Flip_Flop d_ff_2 (.D(d_ff_1_q), .clk(clock), .Q(d_ff_2_q));  // open: Qn, preset, reset
  not not_1 (not_1_out, HLT);
  Decoder #(.select(3)) decoder_1 (
    .out0(t0), .out1(t1), .out2(t2), .out3(t3), .out4(t4), .out5(t5), .out6(t6), .out7(t7),
    .sel(counter_1_q), .en(not_1_out));
endmodule
