// Logisim project top_level.circ as structural Verilog: 1 circuit, main circuit main
module main (
  input  reset
);

  wire ACC_0, ACC_1, ACC_2, ACC_3, ACC_4, ACC_5, ACC_6, ACC_7, clk, control_unity_v2_1_cargaac,
       control_unity_v2_1_carganz, control_unity_v2_1_cargapc, control_unity_v2_1_cargardm,
       control_unity_v2_1_cargarem, control_unity_v2_1_cargari, control_unity_v2_1_incpc,
       control_unity_v2_1_read, control_unity_v2_1_sel, control_unity_v2_1_ulaadd, control_unity_v2_1_ulaand,
       control_unity_v2_1_ulanot, control_unity_v2_1_ulaor, control_unity_v2_1_ulay,
       control_unity_v2_1_write, dec_cu_1_add_op, dec_cu_1_and_op, dec_cu_1_hlt_op, dec_cu_1_jmp_op,
       dec_cu_1_jn_op, dec_cu_1_jz_op, dec_cu_1_lda_op, dec_cu_1_nop_op, dec_cu_1_not_op, dec_cu_1_or_op,
       dec_cu_1_sta_op, dez_a_OUT, dez_b_OUT, dez_c_OUT, dez_d_OUT, dez_e_OUT, dez_f_OUT, dez_g_OUT,
       mem_1_selrdm, N, PC_0, PC_1, PC_2, PC_3, PC_4, PC_5, PC_6, PC_7, RDM_0, RDM_1, RDM_2, RDM_3, RDM_4,
       RDM_5, RDM_6, RDM_7, REM_0, REM_1, REM_2, REM_3, REM_4, REM_5, REM_6, REM_7, ula_n_z_1_n, ula_n_z_1_z,
       un_a_OUT, un_b_OUT, un_c_OUT, un_d_OUT, un_e_OUT, un_f_OUT, un_g_OUT, Z;
  wire [2:0] ula_code_1_sel;
  wire [3:0] flag;
  wire [7:0] mem_1_data_out, mux_8bits_1_out_mux, mux_8bits_2_out_mux, ula_1_output_s;

  dec_cu dec_cu_1 (
    .flag_in(flag), .NOP_op(dec_cu_1_nop_op), .STA_op(dec_cu_1_sta_op), .LDA_op(dec_cu_1_lda_op),
    .ADD_op(dec_cu_1_add_op), .OR_op(dec_cu_1_or_op), .AND_op(dec_cu_1_and_op), .NOT_op(dec_cu_1_not_op),
    .JMP_op(dec_cu_1_jmp_op), .JN_op(dec_cu_1_jn_op), .JZ_op(dec_cu_1_jz_op), .HLT_op(dec_cu_1_hlt_op));
  control_unity_v2 control_unity_v2_1 (
    .NOP_op(dec_cu_1_nop_op), .STA_op(dec_cu_1_sta_op), .LDA_op(dec_cu_1_lda_op), .ADD_op(dec_cu_1_add_op),
    .OR_op(dec_cu_1_or_op), .AND_op(dec_cu_1_and_op), .NOT_op(dec_cu_1_not_op), .JMP_op(dec_cu_1_jmp_op),
    .JN_op(dec_cu_1_jn_op), .JZ_op(dec_cu_1_jz_op), .HLT_op(dec_cu_1_hlt_op), .N(N), .Z(Z), .clock(clk),
    .reset(reset), .cargaPC(control_unity_v2_1_cargapc), .cargaNZ(control_unity_v2_1_carganz),
    .cargaAC(control_unity_v2_1_cargaac), .ulaNOT(control_unity_v2_1_ulanot),
    .ulaAND(control_unity_v2_1_ulaand), .ulaOR(control_unity_v2_1_ulaor), .ulaADD(control_unity_v2_1_ulaadd),
    .ulaY(control_unity_v2_1_ulay), .write(control_unity_v2_1_write), .read(control_unity_v2_1_read),
    .cargaRDM(control_unity_v2_1_cargardm), .sel(control_unity_v2_1_sel), .incPC(control_unity_v2_1_incpc),
    .cargaRI(control_unity_v2_1_cargari), .cargaREM(control_unity_v2_1_cargarem));
  ula_code ula_code_1 (
    .NOT_op(control_unity_v2_1_ulanot), .AND_op(control_unity_v2_1_ulaand), .OR_op(control_unity_v2_1_ulaor),
    .ADD(control_unity_v2_1_ulaadd), .IDENT_op(control_unity_v2_1_ulay), .sel(ula_code_1_sel));
  program_counter program_counter_1 (
    .cargaPC(control_unity_v2_1_cargapc), .incPC(control_unity_v2_1_incpc), .clock(clk), .reset(reset),
    .Pinp({RDM_7, RDM_6, RDM_5, RDM_4, RDM_3, RDM_2, RDM_1, RDM_0}),
    .Count({PC_7, PC_6, PC_5, PC_4, PC_3, PC_2, PC_1, PC_0}));
  ula ula_1 (
    .input_x({ACC_7, ACC_6, ACC_5, ACC_4, ACC_3, ACC_2, ACC_1, ACC_0}),
    .input_y({RDM_7, RDM_6, RDM_5, RDM_4, RDM_3, RDM_2, RDM_1, RDM_0}), .sel(ula_code_1_sel),
    .output_s(ula_1_output_s));
  mux_8bits mux_8bits_1 (
    .inp_1({PC_7, PC_6, PC_5, PC_4, PC_3, PC_2, PC_1, PC_0}),
    .inp_2({RDM_7, RDM_6, RDM_5, RDM_4, RDM_3, RDM_2, RDM_1, RDM_0}), .sel(control_unity_v2_1_sel),
    .out_mux(mux_8bits_1_out_mux));
  mux_8bits mux_8bits_2 (
    .inp_1({ACC_7, ACC_6, ACC_5, ACC_4, ACC_3, ACC_2, ACC_1, ACC_0}), .inp_2(mem_1_data_out),
    .sel(mem_1_selrdm), .out_mux(mux_8bits_2_out_mux));
  ula_n_z ula_n_z_1 (
    .inp_0(ula_1_output_s[0]), .inp_1(ula_1_output_s[1]), .inp_2(ula_1_output_s[2]),
    .inp_3(ula_1_output_s[3]), .inp_4(ula_1_output_s[4]), .inp_5(ula_1_output_s[5]),
    .inp_6(ula_1_output_s[6]), .inp_7(ula_1_output_s[7]), .N(ula_n_z_1_n), .Z(ula_n_z_1_z));
  ACC u_acc_1 (
    .data_input(ula_1_output_s), .enable(control_unity_v2_1_cargaac), .clock(clk), .reset(reset),
    .data_output({ACC_7, ACC_6, ACC_5, ACC_4, ACC_3, ACC_2, ACC_1, ACC_0}));
  R_E_M r_e_m_1 (
    .data_input(mux_8bits_1_out_mux), .enable(control_unity_v2_1_cargarem), .clock(clk), .reset(reset),
    .data_output({REM_7, REM_6, REM_5, REM_4, REM_3, REM_2, REM_1, REM_0}));
  R_D_M r_d_m_1 (
    .data_input(mux_8bits_2_out_mux), .enable(control_unity_v2_1_cargardm), .clock(clk), .reset(reset),
    .data_output({RDM_7, RDM_6, RDM_5, RDM_4, RDM_3, RDM_2, RDM_1, RDM_0}));
  MEM mem_1 (
    .address_i({REM_7, REM_6, REM_5, REM_4, REM_3, REM_2, REM_1, REM_0}), .write(control_unity_v2_1_write),
    .read(control_unity_v2_1_read), .clk(clk),
    .data_in({RDM_7, RDM_6, RDM_5, RDM_4, RDM_3, RDM_2, RDM_1, RDM_0}), .data_out(mem_1_data_out),
    .selRDM(mem_1_selrdm));
  opcode opcode_1 (
    .data_input({RDM_7, RDM_6, RDM_5, RDM_4, RDM_3, RDM_2, RDM_1, RDM_0}),
    .cargaRI(control_unity_v2_1_cargari), .clock(clk), .reset(reset), .flag_out(flag));
  regNZ regnz_1 (
    .enable(control_unity_v2_1_carganz), .clock(clk), .reset(reset), .N_i(ula_n_z_1_z), .Z_i(ula_n_z_1_n),
    .N_o(N), .Z_o(Z));
  LedBar ledbar_1 (
    .led0(ACC_7), .led1(ACC_6), .led2(ACC_5), .led3(ACC_4), .led4(ACC_3), .led5(ACC_2), .led6(ACC_1),
    .led7(ACC_0));
  Clock u_clk (.out(clk));
  LedBar #(.matrixcols(4)) ledbar_2 (.led0(flag[3]), .led1(flag[2]), .led2(flag[1]), .led3(flag[0]));
  LedBar ledbar_3 (
    .led0(PC_7), .led1(PC_6), .led2(PC_5), .led3(PC_4), .led4(PC_3), .led5(PC_2), .led6(PC_1), .led7(PC_0));
  LedBar ledbar_4 (
    .led0(RDM_7), .led1(RDM_6), .led2(RDM_5), .led3(RDM_4), .led4(RDM_3), .led5(RDM_2), .led6(RDM_1),
    .led7(RDM_0));
  LedBar ledbar_5 (
    .led0(REM_7), .led1(REM_6), .led2(REM_5), .led3(REM_4), .led4(REM_3), .led5(REM_2), .led6(REM_1),
    .led7(REM_0));
  div2disp div2disp_1 (
    .n_3(ACC_3), .n_2(ACC_2), .n_1(ACC_1), .n_0(ACC_0), .dez_a(dez_a_OUT), .dez_b(dez_b_OUT),
    .dez_c(dez_c_OUT), .dez_d(dez_d_OUT), .dez_e(dez_e_OUT), .dez_f(dez_f_OUT), .dez_g(dez_g_OUT),
    .un_a(un_a_OUT), .un_b(un_b_OUT), .un_c(un_c_OUT), .un_d(un_d_OUT), .un_e(un_e_OUT), .un_f(un_f_OUT),
    .un_g(un_g_OUT));
  _7_Segment_Display u_7_segment_display_1 (
    .g(dez_g_OUT), .f(dez_f_OUT), .a(dez_a_OUT), .b(dez_b_OUT), .e(dez_e_OUT), .d(dez_d_OUT), .c(dez_c_OUT));  // open: dp
  _7_Segment_Display u_7_segment_display_2 (
    .g(un_g_OUT), .f(un_f_OUT), .a(un_a_OUT), .b(un_b_OUT), .e(un_e_OUT), .d(un_d_OUT), .c(un_c_OUT));  // open: dp

  // Other names for the same wires on the sheet: ACC_data_out[7:0] = {ACC_7, ACC_6, ACC_5, ACC_4, ACC_3, ACC_2, ACC_1, ACC_0};
  //   flag_0 = flag[0]; flag_1 = flag[1]; flag_2 = flag[2]; flag_3 = flag[3];
  //   PC_data_out[7:0] = {PC_7, PC_6, PC_5, PC_4, PC_3, PC_2, PC_1, PC_0};
  //   RDM_o[7:0] = {RDM_7, RDM_6, RDM_5, RDM_4, RDM_3, RDM_2, RDM_1, RDM_0};
  //   REM_o[7:0] = {REM_7, REM_6, REM_5, REM_4, REM_3, REM_2, REM_1, REM_0}

  // Notes on the sheet:
  //   ACC
  //   OP
  //   PC
  //   RDM
  //   REM
  //   OUT
endmodule
