// Logisim project ula.circ as structural Verilog: 1 circuit, main circuit ula
module ula (
  input  [7:0] input_x,
  input  [7:0] input_y,
  input  [2:0] sel,
  output [7:0] output_s
);

  wire [7:0] adder_8bits_1_output_s, and_8_bits_1_output_s, ident_8_bits_1_out_2, not_8_bits_1_out_2,
       or_8_bits_1_output_s;

  adder_8bits adder_8bits_1 (.input_a(input_x), .input_b(input_y), .output_s(adder_8bits_1_output_s));
  or_8_bits or_8_bits_1 (.input_a(input_x), .input_b(input_y), .output_s(or_8_bits_1_output_s));
  and_8_bits and_8_bits_1 (.input_a(input_x), .input_b(input_y), .output_s(and_8_bits_1_output_s));
  not_8_bits not_8_bits_1 (.in_1(input_x), .out_2(not_8_bits_1_out_2));
  ident_8_bits ident_8_bits_1 (.in_1(input_y), .out_2(ident_8_bits_1_out_2));
  Multiplexer #(.select(3), .width(8)) multiplexer_1 (
    .in0(adder_8bits_1_output_s), .in1(or_8_bits_1_output_s), .in2(and_8_bits_1_output_s),
    .in3(not_8_bits_1_out_2), .in4(ident_8_bits_1_out_2), .out(output_s), .sel(sel));  // open: in5, in6, in7
endmodule
