// Logisim project ula_code_g.circ as structural Verilog: 1 circuit, main circuit ula_code
module ula_code (
  input  NOT_op,
  input  AND_op,
  input  OR_op,
  input  ADD,
  input  IDENT_op,
  output [2:0] sel
);

  wire and_1_out, and_2_out, and_3_out, and_4_out, and_5_out, and_6_out, and_7_out, and_8_out, and_9_out,
       and_10_out, and_11_out, and_12_out, and_13_out, and_14_out, and_15_out, and_16_out, and_17_out,
       and_18_out, and_19_out, not_1_out, not_2_out, not_3_out, not_4_out, not_5_out, or_1_out, or_2_out,
       or_3_out, or_4_out, or_5_out, or_6_out, or_7_out, or_8_out, or_9_out, or_11_out, or_12_out, or_14_out,
       or_15_out, or_17_out;

  not not_1 (not_1_out, ADD);
  not not_2 (not_2_out, OR_op);
  not not_3 (not_3_out, AND_op);
  not not_4 (not_4_out, NOT_op);
  not not_5 (not_5_out, IDENT_op);
  and and_1 (and_1_out, not_1_out, not_2_out);
  and and_2 (and_2_out, not_3_out, not_4_out);
  and and_3 (and_3_out, not_1_out, not_2_out);
  and and_4 (and_4_out, not_1_out, not_3_out);
  and and_5 (and_5_out, and_1_out, and_2_out);
  and and_6 (and_6_out, AND_op, NOT_op);
  and and_7 (and_7_out, OR_op, NOT_op);
  and and_8 (and_8_out, OR_op, AND_op);
  and and_9 (and_9_out, ADD, NOT_op);
  and and_10 (and_10_out, ADD, AND_op);
  and and_11 (and_11_out, ADD, OR_op);
  and and_12 (and_12_out, and_3_out, not_5_out);
  and and_13 (and_13_out, OR_op, IDENT_op);
  and and_14 (and_14_out, ADD, IDENT_op);
  and and_15 (and_15_out, and_4_out, not_5_out);
  and and_16 (and_16_out, ADD, IDENT_op);
  or or_1 (or_1_out, and_5_out, IDENT_op);
  or or_2 (or_2_out, and_6_out, and_7_out);
  or or_3 (or_3_out, and_8_out, and_9_out);
  or or_4 (or_4_out, and_10_out, and_11_out);
  or or_5 (or_5_out, and_12_out, NOT_op);
  or or_6 (or_6_out, and_13_out, and_14_out);
  and and_17 (and_17_out, ADD, OR_op);
  or or_7 (or_7_out, and_15_out, NOT_op);
  and and_18 (and_18_out, AND_op, IDENT_op);
  or or_8 (or_8_out, OR_op, and_16_out);
  and and_19 (and_19_out, ADD, AND_op);
  or or_9 (or_9_out, or_1_out, or_2_out);
  or or_10 (sel[2], or_9_out, or_11_out);
  or or_11 (or_11_out, or_3_out, or_4_out);
  or or_12 (or_12_out, or_5_out, AND_op);
  or or_13 (sel[1], or_12_out, or_14_out);
  or or_14 (or_14_out, or_6_out, and_17_out);
  or or_15 (or_15_out, or_7_out, and_18_out);
  or or_16 (sel[0], or_15_out, or_17_out);
  or or_17 (or_17_out, or_8_out, and_19_out);
endmodule
