// Logisim project ula_n_z.circ as structural Verilog: 1 circuit, main circuit ula_n_z
module ula_n_z (
  input  inp_0,
  input  inp_1,
  input  inp_2,
  input  inp_3,
  input  inp_4,
  input  inp_5,
  input  inp_6,
  input  inp_7,
  output N,
  output Z
);

  nor nor_1 (Z, inp_7, inp_6, inp_5, inp_4, inp_3, inp_2, inp_1, inp_0);

  assign N = inp_7;
endmodule
